# Fritzing sketch quack-alternative (saved by Fritzing 0.9.4)
stripboards: 2

parts:
  Bauteil1 = Arduino Mega 2560 (Rev3)
  S1 = Pushbutton [package=THT]
  S2 = Pushbutton [package=THT]
  S3 = Pushbutton [package=THT]
  S4 = Pushbutton [package=THT]
  S5 = Pushbutton [package=THT]
  S6 = Pushbutton [package=THT]
  S7 = Pushbutton [package=THT]
  Bauteil2 = Arduino Mega 2560 (Rev3)
  LED1 = LED - 5mm [color="White (4500K)" package="5 mm [THT]"]
  R1 = Resistor [tolerance=±5% resistance=220 package=THT]
  LED2 = LED - 5mm [color="White (4500K)" package="5 mm [THT]"]
  R2 = Resistor [tolerance=±5% resistance=220 package=THT]
  LED3 = LED - 5mm [color="White (4500K)" package="5 mm [THT]"]
  R3 = Resistor [tolerance=±5% resistance=220 package=THT]
  LED4 = LED - 5mm [color="White (4500K)" package="5 mm [THT]"]
  R4 = Resistor [tolerance=±5% resistance=220 package=THT]
  LED5 = LED - 5mm [color="White (4500K)" package="5 mm [THT]"]
  R5 = Resistor [tolerance=±5% resistance=220 package=THT]
  LED6 = LED - 5mm [color="White (4500K)" package="5 mm [THT]"]
  R6 = Resistor [tolerance=±5% resistance=220 package=THT]
  LED7 = LED - 5mm [color="White (4500K)" package="5 mm [THT]"]
  R7 = Resistor [tolerance=±5% resistance=220 package=THT]

nets:
  N1: Bauteil1.GND, S1.leg0, S2.leg0, S3.leg0, S4.leg0, S5.leg0, S6.leg0, S7.leg0
  N2: Bauteil1.D23, S1.leg1
  N3: Bauteil1.D25, S2.leg1
  N4: Bauteil1.D27, S3.leg1
  N5: Bauteil1.D29, S4.leg1
  N6: Bauteil1.D31, S5.leg1
  N7: Bauteil1.D33, S6.leg1
  N8: Bauteil1.D35, S7.leg1
  N9: Bauteil2.D41, R7.Pin_1
  N10: Bauteil2.D43, R6.Pin_1
  N11: Bauteil2.D45, R5.Pin_1
  N12: Bauteil2.D47, R4.Pin_1
  N13: Bauteil2.D49, R3.Pin_1
  N14: Bauteil2.D51, R2.Pin_1
  N15: Bauteil2.D53, R1.Pin_1
  N16: Bauteil2.GND, LED1.cathode, LED2.cathode, LED3.cathode, LED4.cathode, LED5.cathode, LED6.cathode, LED7.cathode
  N17: LED1.anode, R1.Pin_0
  N18: LED2.anode, R2.Pin_0
  N19: LED3.anode, R3.Pin_0
  N20: LED4.anode, R4.Pin_0
  N21: LED5.anode, R5.Pin_0
  N22: LED6.anode, R6.Pin_0
  N23: LED7.anode, R7.Pin_0

notes:
  repeat 7 times
  Solder Points Count:
  >> Per Button: 3 x 49 147
  >> >> to Button 1
  >> >> to Bank 2
  >> Bank to Ground 1
  >> Per LED: 5 x 49 245
  >> >> to Resistor 1
  >> >> to LED 2
  >> >> to Bank 2
  >> Bank to Ground 2
  TOTAL: 395
  Extensibility:
  Not possible, 49 buttons / LEDs per Arduino is the maximum
