# Fritzing sketch quack (saved by Fritzing 0.9.4)
stripboards: 7

parts:
  Bauteil1 = Arduino Mega 2560 (Rev3)
  S2 = Pushbutton [package=THT]
  D2 = Rectifier Diode [part_number=1N4001 package="300 mil [THT]"]
  S3 = Pushbutton [package=THT]
  D3 = Rectifier Diode [part_number=1N4001 package="300 mil [THT]"]
  S4 = Pushbutton [package=THT]
  D4 = Rectifier Diode [part_number=1N4001 package="300 mil [THT]"]
  S5 = Pushbutton [package=THT]
  S6 = Pushbutton [package=THT]
  S7 = Pushbutton [package=THT]
  S8 = Pushbutton [package=THT]
  D5 = Rectifier Diode [part_number=1N4001 package="300 mil [THT]"]
  D6 = Rectifier Diode [part_number=1N4001 package="300 mil [THT]"]
  D7 = Rectifier Diode [part_number=1N4001 package="300 mil [THT]"]
  D8 = Rectifier Diode [part_number=1N4001 package="300 mil [THT]"]
  LED33 = LED - 5mm [color="White (4500K)" package="5 mm [THT]"]
  R_LED = Resistor [tolerance=±5% resistance=100 package=THT]
  LED34 = LED - 5mm [color="White (4500K)" package="5 mm [THT]"]
  LED35 = LED - 5mm [color="White (4500K)" package="5 mm [THT]"]
  LED36 = LED - 5mm [color="White (4500K)" package="5 mm [THT]"]
  LED37 = LED - 5mm [color="White (4500K)" package="5 mm [THT]"]
  LED38 = LED - 5mm [color="White (4500K)" package="5 mm [THT]"]
  LED_(3V_20mA) = LED - 5mm [color="White (4500K)" package="5 mm [THT]"]
  LED39 = LED - 5mm [color="White (4500K)" package="5 mm [THT]"]
  LED40 = LED - 5mm [color="White (4500K)" package="5 mm [THT]"]
  LED41 = LED - 5mm [color="White (4500K)" package="5 mm [THT]"]
  LED42 = LED - 5mm [color="White (4500K)" package="5 mm [THT]"]
  3V_20mA1 = LED - 5mm [color="White (4500K)" package="5 mm [THT]"]
  LED43 = LED - 5mm [color="White (4500K)" package="5 mm [THT]"]
  LED44 = LED - 5mm [color="White (4500K)" package="5 mm [THT]"]
  R2 = Resistor [tolerance=±5% resistance=100 package=THT]
  U5 = mystery part, 4 pins [chip_label=...]
  U1 = mystery part, 4 pins [chip_label=...]
  U2 = mystery part, 4 pins [chip_label=...]
  U3 = mystery part, 4 pins [chip_label=...]
  U4 = mystery part, 4 pins [chip_label=...]
  S9 = Pushbutton [package=THT]
  S10 = Pushbutton [package=THT]
  S11 = Pushbutton [package=THT]
  S12 = Pushbutton [package=THT]
  S13 = Pushbutton [package=THT]
  S14 = Pushbutton [package=THT]
  S15 = Pushbutton [package=THT]
  D9 = Rectifier Diode [part_number=1N4001 package="300 mil [THT]"]
  D10 = Rectifier Diode [part_number=1N4001 package="300 mil [THT]"]
  D11 = Rectifier Diode [part_number=1N4001 package="300 mil [THT]"]
  D12 = Rectifier Diode [part_number=1N4001 package="300 mil [THT]"]
  D13 = Rectifier Diode [part_number=1N4001 package="300 mil [THT]"]
  D14 = Rectifier Diode [part_number=1N4001 package="300 mil [THT]"]
  D15 = Rectifier Diode [part_number=1N4001 package="300 mil [THT]"]
  U6 = mystery part, 4 pins [chip_label=...]
  U7 = mystery part, 4 pins [chip_label=...]
  U8 = mystery part, 4 pins [chip_label=...]
  U9 = mystery part, 4 pins [chip_label=...]
  U10 = mystery part, 4 pins [chip_label=...]
  R_Button_GND = Resistor [tolerance=±5% resistance=10M package=THT]
  R_Button_2 = Resistor [tolerance=±5% resistance=10M package=THT]
  D16 = Rectifier Diode [part_number=1N4001 package="300 mil [THT]"]
  D17 = Rectifier Diode [part_number=1N4001 package="300 mil [THT]"]
  D18 = Rectifier Diode [part_number=1N4001 package="300 mil [THT]"]
  D19 = Rectifier Diode [part_number=1N4001 package="300 mil [THT]"]
  D20 = Rectifier Diode [part_number=1N4001 package="300 mil [THT]"]
  D21 = Rectifier Diode [part_number=1N4001 package="300 mil [THT]"]
  D22 = Rectifier Diode [part_number=1N4001 package="300 mil [THT]"]

nets:
  N1: Bauteil1.GND, R_Button_2.Pin_1
  N2: Bauteil1.D22, D7.cathode, D10.cathode, D22.anode
  N3: Bauteil1.D23, S2.leg0, S3.leg0, S4.leg0, S5.leg0, S6.leg0, S7.leg0, S8.leg0
  N4: Bauteil1.D24, D8.cathode, D9.cathode, D21.anode
  N5: Bauteil1.D25, S9.leg0, S10.leg0, S11.leg0, S12.leg0, S13.leg0, S14.leg0, S15.leg0
  N6: Bauteil1.D26, D6.cathode, D11.cathode, D20.anode
  N7: Bauteil1.D27, U9.pin1
  N8: Bauteil1.D28, D5.cathode, D12.cathode, D19.anode
  N9: Bauteil1.D29, U8.pin1
  N10: Bauteil1.D30, D4.cathode, D13.cathode, D18.anode
  N11: Bauteil1.D31, U7.pin1
  N12: Bauteil1.D32, D3.cathode, D14.cathode, D17.anode
  N13: Bauteil1.D33, U6.pin1
  N14: Bauteil1.D34, D2.cathode, D15.cathode, D16.anode
  N15: Bauteil1.D35, U10.pin1
  N16: Bauteil1.D40, LED_(3V_20mA).cathode, 3V_20mA1.cathode
  N17: Bauteil1.D41, U5.pin4
  N18: Bauteil1.D42, LED38.cathode, LED41.cathode
  N19: Bauteil1.D43, U4.pin4
  N20: Bauteil1.D44, LED37.cathode, LED39.cathode
  N21: Bauteil1.D45, U3.pin4
  N22: Bauteil1.D46, LED36.cathode, LED42.cathode
  N23: Bauteil1.D47, U2.pin4
  N24: Bauteil1.D48, LED35.cathode, LED44.cathode
  N25: Bauteil1.D49, U1.pin4
  N26: Bauteil1.D50, LED34.cathode, LED40.cathode
  N27: Bauteil1.D51, R2.Pin_0
  N28: Bauteil1.D52, LED33.cathode, LED43.cathode
  N29: Bauteil1.D53, R_LED.Pin_0
  N30: S2.leg1, D2.anode
  N31: S3.leg1, D3.anode
  N32: S4.leg1, D4.anode
  N33: S5.leg1, D5.anode
  N34: S6.leg1, D6.anode
  N35: S7.leg1, D7.anode
  N36: S8.leg1, D8.anode
  N37: LED33.anode, R_LED.Pin_1, LED34.anode, LED35.anode, LED36.anode, LED37.anode, LED38.anode, LED_(3V_20mA).anode
  N38: LED39.anode, LED40.anode, LED41.anode, LED42.anode, 3V_20mA1.anode, LED43.anode, LED44.anode, R2.Pin_1
  N39: S9.leg1, D9.anode
  N40: S10.leg1, D10.anode
  N41: S11.leg1, D11.anode
  N42: S12.leg1, D12.anode
  N43: S13.leg1, D13.anode
  N44: S14.leg1, D14.anode
  N45: S15.leg1, D15.anode
  N46: R_Button_GND.Pin_0, R_Button_GND.Pin_1, R_Button_2.Pin_0, D16.cathode, D17.cathode, D18.cathode, D19.cathode, D20.cathode, D21.cathode, D22.cathode

notes:
  based on https://learn.sparkfun.com/tutorials/button-pad-hookup-guide
  repeat accordingly
  columns repeated accordingly
