# Fritzing sketch quacking_testing (saved by Fritzing 0.9.4)
breadboards: 1

parts:
  Bauteil1 = Arduino Mega 2560 (Rev3)
  S1 = Round Pushbutton
  R1 = Resistor [tolerance=±5% resistance=10M package=THT]
  S2 = Round Pushbutton
  D1 = Rectifier Diode [part_number=1N4001 package="300 mil [THT]"]
  D2 = Rectifier Diode [part_number=1N4001 package="300 mil [THT]"]

nets:
  N1: Bauteil1.GND, R1.Pin_0
  N2: Bauteil1.D9_PWM, S2.leg1, D1.anode
  N3: Bauteil1.D8_PWM, S1.leg0, D2.anode
  N4: Bauteil1.D7_PWM, S1.leg1, S2.leg0
  N5: R1.Pin_1, D1.cathode, D2.cathode

notes:
  So basically
  I'm a duck
  *quack*
